# Fritzing sketch Updated UPS Final (saved by Fritzing 0.9.3b)
# 18650 Li-ion Battery: CC-BY Dr Kristofer Chan, King's College London/Remote-research.org

parts:
  Mod3 = 3S-BMS
  A2 = WMYCONGCONG buck converter
  J1 = Power Jack [package=power_jack_combo]
  S1 = Round Pushbutton
  LED1 = smd LED [color="Red (633nm)" package="1206 [SMD]"]
  R1 = Resistor [tolerance=±5% resistance=220 package=THT]  # not connected
  D1 = Rectifier Diode [part_number=1N4001 package="300 mil [THT]"]
  J2 = Power Jack [package=power_jack_combo]
  BAT4 = 18650 Li-ion Battery [package=battery-18650]
  BAT5 = 18650 Li-ion Battery [package=battery-18650]
  BAT6 = 18650 Li-ion Battery [package=battery-18650]

nets:
  N1: Mod3.0V, BAT4.+
  N2: Mod3.4.2V, BAT4.-, BAT5.+
  N3: Mod3.8.4V, BAT5.-, BAT6.+
  N4: Mod3.-, A2.Pin_3, LED1.cathode, J2.GND
  N5: Mod3.+, S1.leg0, D1.cathode
  N6: Mod3.12.6V, BAT6.-
  N7: A2.Pin_1, J1.GND
  N8: A2.Pin_2, S1.leg1
  N9: A2.Pin_4, J1.GNDBREAK

custom parts:
  3S-BMS: 3S-BMS LIPO battery charger / protection unit. Note pcb does not match the board as it will likely connect with wires, so pcb is 6 pads suitable for .1in header pins.
  WMYCONGCONG buck converter: These amazing little DC-DC converters feature a wide input voltage of 4.5-24V and the output voltage can be set to one of six fixed voltages, or fully variable, just by bridging the relevant solder pads on the back of the PCB..
  Round Pushbutton: A generic pushbutton.
  18650 Li-ion Battery: 18650 li-ion Battery Standard 18650 battery with interactive connectors Creative Common Attribution 4.0 International (CC-BY 4.0) license. Any use of this part requires attribution of Dr Kristofer Chan, Department of Geography, King's College London. Contact kristofer.chan [at] kcl.ac.uk OR kris [at] remote-research.org for further information.
